// Logisim project timer_.circ as structural Verilog: 3 circuits, main circuit Timer
module main (
  input  [3:0] boutons,
  input  [2:0] etat,
  input  [22:0] temps,
  output sous_systeme,
  output [22:0] temps_set,
  output [22:0] temps_restant,
  output sonne
);

  wire actif_q, and_1_out, and_2_out, and_3_out, and_4_out, and_5_out, and_6_out, and_7_out, and_8_out,
       and_9_out, and_10_out, and_12_out, comparator_1_eq, comparator_2_eq, d_ff_2_q, d_ff_3_q, d_ff_4_q,
       not_1_out, or_1_out, subtractor_1_bout;
  wire [1:0] or_2_out;
  wire [22:0] adder_1_out, duree_q, fin_q, multiplexer_1_out, multiplexer_2_out, register_1_q,
       subtractor_1_out, subtractor_2_out;

  Comparator #(.width(3), .mode("unsigned")) comparator_1 (.a(etat), .b(3'b011), .eq(comparator_1_eq));  // open: gt, lt
  D_Flip_Flop d_ff_1 (.D(1'b1), .clk(and_1_out), .Q(sous_systeme), .reset(and_3_out));  // open: Qn, preset
  and and_1 (and_1_out, boutons[1], ~actif_q, comparator_1_eq);  // AND_Gate
  and and_2 (and_2_out, boutons[2], ~sous_systeme, comparator_1_eq);  // AND_Gate
  and and_3 (and_3_out, sous_systeme, boutons[1], comparator_1_eq, ~and_1_out);  // AND_Gate
  or or_1 (or_1_out, and_2_out, 1'b0);
  T_Flip_Flop actif (.T(comparator_1_eq), .clk(or_1_out), .Q(actif_q));  // open: Qn, reset, preset
  and and_4 (and_4_out, sous_systeme, ~d_ff_2_q);  // AND_Gate
  D_Flip_Flop d_ff_2 (.D(sous_systeme), .clk(boutons[2]), .Q(d_ff_2_q), .reset(d_ff_4_q));  // open: Qn, preset
  Register #(.width(23)) duree (.D(register_1_q), .clk(and_3_out), .Q(duree_q));  // open: en, clr
  and and_5 (and_5_out, boutons[2], actif_q);
  and and_6 (and_6_out, d_ff_2_q, ~d_ff_3_q);  // AND_Gate
  D_Flip_Flop d_ff_3 (.D(d_ff_2_q), .clk(boutons[2]), .Q(d_ff_3_q), .reset(d_ff_4_q));  // open: Qn, preset
  Register #(.width(23)) debut (.D(temps), .clk(and_5_out));  // open: en, Q, clr
  and and_7 (and_7_out, d_ff_3_q, ~d_ff_4_q);  // AND_Gate
  D_Flip_Flop d_ff_4 (.D(d_ff_3_q), .clk(boutons[2]), .Q(d_ff_4_q), .reset(d_ff_4_q));  // open: Qn, preset
  Adder #(.width(23)) adder_1 (.a(duree_q), .b(temps), .out(adder_1_out));  // open: cin, cout
  Subtractor #(.width(23)) subtractor_1 (
    .a(adder_1_out), .b(23'h5c4900), .out(subtractor_1_out), .bout(subtractor_1_bout));  // open: bin
  Register #(.width(23)) fin (.D(multiplexer_1_out), .clk(and_5_out), .Q(fin_q));  // open: en, clr
  Multiplexer #(.width(23), .enable("false")) multiplexer_1 (
    .in0(subtractor_1_out), .in1(adder_1_out), .out(multiplexer_1_out), .sel(subtractor_1_bout));
  and and_8 (and_8_out, and_4_out, boutons[0]);
  and and_9 (and_9_out, and_6_out, boutons[0]);
  and and_10 (and_10_out, and_7_out, boutons[0]);
  Comparator #(.width(23), .mode("unsigned")) comparator_2 (
    .a(fin_q), .b(temps), .eq(comparator_2_eq));  // open: gt, lt
  or or_2 (or_2_out[0], and_8_out, and_10_out);
  or or_3 (or_2_out[1], and_9_out, and_10_out);
  and and_11 (sonne, comparator_2_eq, actif_q);
  Multiplexer #(.select(2), .width(23), .enable("false")) multiplexer_2 (
    .in0({23{1'b0}}), .in1(23'h8ca0), .in2(23'h1770), .in3(23'h258), .out(multiplexer_2_out), .sel(or_2_out));
  Subtractor #(.width(23)) subtractor_2 (.a(fin_q), .b(temps), .out(subtractor_2_out));  // open: bin, bout
  Adder #(.width(23)) adder_2 (.a(multiplexer_2_out), .b(register_1_q), .out(temps_set));  // open: cin, cout
  not not_1 (not_1_out, boutons[0]);
  Multiplexer #(.width(23), .enable("false")) multiplexer_3 (
    .in0(duree_q), .in1(subtractor_2_out), .out(temps_restant), .sel(actif_q));
  Register #(.width(23)) register_1 (.D(temps_set), .clk(not_1_out), .Q(register_1_q), .clr(and_12_out));  // open: en
  and and_12 (and_12_out, sous_systeme, and_1_out);

  // Notes on the sheet:
  //   mode set
  //   reset (inutile ?)
  //   ceci est inutile également
endmodule

module Timer (
  input  [3:0] Boutons,
  input  [2:0] Etat,
  input  [22:0] Temps
);

  wire comparator_1_eq;

  Comparator #(.width(3)) comparator_1 (.a(Etat), .b(3'b011), .eq(comparator_1_eq));  // open: gt, lt
endmodule

module T_affiche (
  input  [22:0] temps_restant
);
endmodule
